// Logisim project proiectpsnas.circ as structural Verilog
module main (
  input  Input_1,
  output [6:0] out_2,
  output [6:0] out_3,
  output [3:0] Output_bus_1,
  output [6:0] out_5,
  output [1:0] Output_bus_2
);

  wire Button_1_out, Button_2_out, Button_3_out, cifru_1_rez, clock_1_out, d_ff_1_q, d_ff_1_qn, uc_1_en_cmp1,
       uc_1_introdu_caractere_led, uc_1_introdus_3_led, uc_1_liber_ocupat_led;
  wire [3:0] cifru_1_cif1_a, cifru_1_cif2_a, cifru_1_cif3_a, demultiplexer_1_out0, demultiplexer_1_out1,
       demultiplexer_1_out2;

  Clock clock_1 (.out(clock_1_out));
  Button Button_1 (.out(Button_1_out));
  Button Button_2 (.out(Button_2_out));
  Button Button_3 (.out(Button_3_out));
  D_Flip_Flop d_ff_1 (.D(Button_3_out), .clk(clock_1_out), .Q(d_ff_1_q), .Qn(d_ff_1_qn), .preset(1'b0), .reset(1'b0));
  counter counter_1 (.C(clock_1_out), .up(Button_1_out), .down(Button_2_out), .reset(d_ff_1_q), .Q(Output_bus_1));
  LED LED_1 (.in(uc_1_introdus_3_led));
  UC uc_1 (
    .up(Button_1_out), .down(Button_2_out), .reset(Input_1), .adauga_cifru(Button_3_out), .clk(clock_1_out),
    .cmp_3(cifru_1_rez), .introdus_3_LED(uc_1_introdus_3_led),
    .introdu_caractere_LED(uc_1_introdu_caractere_led), .liber_ocupat_LED(uc_1_liber_ocupat_led),
    .sel_afisor(Output_bus_2), .en_cmp1(uc_1_en_cmp1));
  LED LED_3 (.in(uc_1_liber_ocupat_led));
  LED LED_2 (.in(uc_1_introdu_caractere_led));
  Demultiplexer #(.select(2), .width(4)) demultiplexer_1 (
    .out0(demultiplexer_1_out0), .out1(demultiplexer_1_out1), .out2(demultiplexer_1_out2), .in(Output_bus_1),
    .sel(Output_bus_2));  // open: out3
  Hex_Digit_Display Hex_Digit_Display_2 (.value(cifru_1_cif2_a));  // open: dp
  Hex_Digit_Display Hex_Digit_Display_1 (.value(cifru_1_cif3_a));  // open: dp
  Hex_Digit_Display Hex_Digit_Display_4 (.value(demultiplexer_1_out2));  // open: dp
  Hex_Digit_Display Hex_Digit_Display_3 (.value(cifru_1_cif1_a));  // open: dp
  Hex_Digit_Display Hex_Digit_Display_5 (.value(demultiplexer_1_out1));  // open: dp
  Hex_Digit_Display Hex_Digit_Display_6 (.value(demultiplexer_1_out0));  // open: dp
  cifru cifru_1 (
    .cif(Output_bus_1), .sel(Output_bus_2), .mode(uc_1_liber_ocupat_led), .en_cmp(uc_1_en_cmp1),
    .rez(cifru_1_rez), .cif1_a(cifru_1_cif1_a), .cif2_a(cifru_1_cif2_a), .cif3_a(cifru_1_cif3_a));
  HEX2Seg hex2seg_1 (.hex(cifru_1_cif1_a), .seg(out_2));
  HEX2Seg hex2seg_2 (.hex(cifru_1_cif2_a), .seg(out_3));
  HEX2Seg hex2seg_3 (.hex(cifru_1_cif3_a), .seg(out_5));
endmodule

// VHDL entity UC, as the project stores it:
--------------------------------------------------------------------------------
-- Project :
-- File    :
-- Autor   :
-- Date    :
--
--------------------------------------------------------------------------------
-- Description :
--
--------------------------------------------------------------------------------

LIBRARY ieee;
USE ieee.std_logic_1164.all;

ENTITY UC IS
  PORT (
  		up,down,reset,adauga_cifru : in std_logic;
    		clk : in std_logic;
    		introdus_3_LED : out std_logic;
    		cmp_3 : in std_logic;
    		introdu_caractere_LED,liber_ocupat_LED : out std_logic;
    		sel_afisor : out std_logic_vector (1 downto 0);
    		en_cmp1 : out std_logic
    		
    );
END UC;

--------------------------------------------------------------------------------
--Complete your VHDL description below
--------------------------------------------------------------------------------

ARCHITECTURE TypeArchitecture OF UC IS

type STATE_dai is (idle, dulap_liber, car_1, car_2, car_3,cifru_adaugat,dulap_ocupat, car_1_o, car_2_o, car_3_o,cifru_adaugat_o,verif);
signal STATE, NXSTATE: STATE_dai;
signal introdu_caractere,liber_ocupat,introdus_3: std_logic :='0';
BEGIN

UPDATE_STATE: process (Clk)
			begin
			if Clk'EVENT and Clk = '1' then
					STATE <= NXSTATE;
				end if;
			end process UPDATE_STATE;

TRANSITIONS: process (STATE,adauga_cifru,reset,cmp_3,liber_ocupat)
				
				begin
				case STATE is
					when idle => en_cmp1<='0';
								if liber_ocupat='1' then NXSTATE<=dulap_ocupat;
								else NXSTATE <= dulap_liber;
								end if;
					when dulap_liber => if adauga_cifru='1' then NXSTATE <= car_1;
							   else NXSTATE <= dulap_liber;
							   end if;
					when car_1 => sel_afisor<="00";
								if adauga_cifru='1' then NXSTATE <= car_2;
								 else NXSTATE <= car_1;
								 end if;
					when car_2 => sel_afisor<="01";
								if adauga_cifru='1' then NXSTATE <= car_3;
								 else NXSTATE <= car_2;
								 end if;
					when car_3 => sel_afisor<="10";
								if adauga_cifru='1' then NXSTATE <= cifru_adaugat;
								 else NXSTATE <= car_3;
								 end if;
					when cifru_adaugat =>  sel_afisor<="11";
								if reset='1' then NXSTATE <= dulap_liber;
								else NXSTATE <= dulap_ocupat;
								end if;
									
					when dulap_ocupat => if adauga_cifru='1' then NXSTATE <= car_1_o;
							   else NXSTATE <= dulap_ocupat;
							   end if;
					when car_1_o => sel_afisor<="00";
								if adauga_cifru='1' then NXSTATE <= car_2_o;
								 else NXSTATE <= car_1_o;
								 end if;
					when car_2_o => sel_afisor<="01";
								if adauga_cifru='1' then NXSTATE <= car_3_o;
								 else NXSTATE <= car_2_o;
								 end if;
					when car_3_o => sel_afisor<="10";
								if adauga_cifru='1' then NXSTATE <= cifru_adaugat_o;
								 else NXSTATE <= car_3_o;
								 end if;
					when cifru_adaugat_o => sel_afisor<="11";
								if reset='1' then NXSTATE <= dulap_ocupat;
								else NXSTATE <= verif;
								end if;
					when verif => 	en_cmp1<='1';
								if cmp_3='1' then NXSTATE <= dulap_liber;
									else NXSTATE <= dulap_ocupat;
									end if;						
				end case;
			end process;

			
Outputs: process (STATE,adauga_cifru,reset,cmp_3,liber_ocupat)
		begin


		case STATE is
					when idle => introdu_caractere_LED<='0' ; liber_ocupat_LED<='0'; introdus_3_LED<='0';
					when dulap_liber => introdu_caractere_LED<='1';en_cmp1<='0';
					when cifru_adaugat => if reset='0' then introdu_caractere_LED<='0';liber_ocupat_LED<='1';introdus_3_LED<='1';
									  else introdu_caractere_LED<='1';
									  end if;
					when dulap_ocupat => introdu_caractere_LED<='1';introdus_3_LED<='0';
					when cifru_adaugat_o => if reset='0' then introdu_caractere_LED<='0';introdus_3_LED<='1';
									 else introdu_caractere_LED<='1';
									 end if;
					when verif => 
								if cmp_3='1' then liber_ocupat_LED<='0';introdus_3_LED<='0';
								else liber_ocupat_LED<='1';introdus_3_LED<='0';
								END if;
					when others => introdus_3_LED<='0';
				end case;	
		end process;	


END TypeArchitecture;

// VHDL entity counter, as the project stores it:
library ieee;
use ieee.std_logic_1164.all; 
use ieee.std_logic_unsigned.all; 
 
entity counter is 
  port(C,up,down,reset: in  std_logic;  
        Q : out std_logic_vector(3 downto 0));  
end counter; 

architecture archi of counter is  
  signal tmp: std_logic_vector(3 downto 0):="0000"; 
  begin  
      process (C,up,down) 
        begin  
        if reset='1' then
        	tmp<="0000";
        else
  		if up='1' and down='0' then
  			if (tmp="1111") then  
            		tmp <= "0000";  
            	elsif (C'event and C='1') then
            		tmp <= tmp + 1;
            	end if;
          elsif up='0' and down='1' then
            	if (tmp="0000") then  
            		tmp <= "1111";  
            	elsif (C'event and C='1') then
            		tmp <= tmp - 1;
            	end if;
          end if;
          end if;
      end process; 
      Q <= tmp;  
end archi;

// VHDL entity cifru, as the project stores it:
--------------------------------------------------------------------------------
-- Project :
-- File    :
-- Autor   :
-- Date    :
--
--------------------------------------------------------------------------------
-- Description :
--
--------------------------------------------------------------------------------

LIBRARY ieee;
USE ieee.std_logic_1164.all;

ENTITY cifru IS
  PORT (
  		cif : in std_logic_vector (3 downto 0);
		sel : in std_logic_vector (1 downto 0);
		mode : in  std_logic;
		en_cmp : in std_logic;
		rez : out std_logic;
		cif1_a,cif2_a,cif3_a : out std_logic_vector (3 downto 0) --cif pt afisat
    );
END cifru;

--------------------------------------------------------------------------------
--Complete your VHDL description below
--------------------------------------------------------------------------------

ARCHITECTURE TypeArchitecture OF cifru IS
signal cif1_c,cif2_c,cif3_c: std_logic_vector (3 downto 0); -- cif curente
signal cif1,cif2,cif3: std_logic_vector (3 downto 0); -- cif din dulap


BEGIN

process (en_cmp,mode,sel,cif,cif1,cif2,cif3)
begin
	if en_cmp='0' then
		if mode='0' then --introducem cod
			case sel is
				when "00"=> cif1<=cif;cif1_a<=cif1;
				when "01"=> cif2<=cif;cif2_a<=cif2;
				when "10"=> cif3<=cif;cif3_a<=cif3;
				when others => rez<='0';
			end case;
		else 
			case sel is
				when "00"=> cif1_c<=cif;
				when "01"=> cif2_c<=cif;
				when "10"=> cif3_c<=cif;
				when others => rez<='0';
			end case;
		end if;
	else 
		if cif1=cif1_c and cif2=cif2_c and cif3=cif3_c then
			rez<='1';
		else
			rez<='0';
		end if;
	end if;
			
end process;
END TypeArchitecture;

// VHDL entity HEX2Seg, as the project stores it:
library IEEE;
use IEEE.STD_LOGIC_1164.ALL;

entity HEX2Seg is
    Port ( hex : in STD_LOGIC_VECTOR (3 downto 0);
           seg : out STD_LOGIC_VECTOR (6 downto 0)
           );
           
end HEX2Seg;

architecture Behavioral of HEX2Seg is

begin
seg(6 downto 0) <=
        --  gfedcba 
           "1000000" when HEX="0000" else--0
           "1001111" when HEX="0001" else--1
           "0100100" when HEX="0010" else--2
           "0110000" when HEX="0011" else--3
           "0011001" when HEX="0100" else--4
           "0010010" when HEX="0101" else--5
           "0000010" when HEX="0110" else--6
           "1111000" when HEX="0111" else--7
           "0000000" when HEX="1000" else--8
           "0010000" when HEX="1001" else--9
           "0001000" when HEX="1010" else--A
           "0000011" when HEX="1011" else--b
           "1000110" when HEX="1100" else--C
           "0100001" when HEX="1101" else--d
           "0000110" when HEX="1110" else--E
           "0001110" when HEX="1111" else--F
           "0000000";       
end Behavioral;

// VHDL entity main_bun, as the project stores it:
--------------------------------------------------------------------------------
-- Project :
-- File    :
-- Autor   :
-- Date    :
--
--------------------------------------------------------------------------------
-- Description :
--
--------------------------------------------------------------------------------

LIBRARY ieee;
USE ieee.std_logic_1164.all;

ENTITY main_bun IS
  PORT (
	Mup,Mdown,Mreset,Madauga_cifra,Mclk: in std_logic;
	Mintrodus_3,Mintrodu_cifre,Mliber_ocupat:out std_logic;
	cif1: out std_logic_vector(6 downto 0)
    );
END main_bun;

--------------------------------------------------------------------------------
--Complete your VHDL description below
--------------------------------------------------------------------------------

ARCHITECTURE TypeArchitecture OF main_bun IS

component UC IS
  PORT (
  		up,down,reset,adauga_cifru : in std_logic;
    		clk : in std_logic;
    		introdus_3_LED : out std_logic;
    		cmp_3 : in std_logic;
    		introdu_caractere_LED,liber_ocupat_LED : out std_logic;
    		sel_afisor : out std_logic_vector (1 downto 0);
    		en_cmp1 : out std_logic
    		
    );
END component;


component counter is 
  port(C,up,down,reset: in  std_logic;  
        Q : out std_logic_vector(3 downto 0));  
END component;

component cifru IS
  PORT (
  		cif : in std_logic_vector (3 downto 0);
		sel : in std_logic_vector (1 downto 0);
		mode : in  std_logic;
		en_cmp : in std_logic;
		rez : out std_logic;
		cif1_a,cif2_a,cif3_a : out std_logic_vector (3 downto 0)
    );
END component;


component HEX2Seg is
    Port ( hex : in STD_LOGIC_VECTOR (3 downto 0);
           seg : out STD_LOGIC_VECTOR (6 downto 0)
          );
END component;

signal q_counter: std_logic_vector(3 downto 0);
signal rez_cifru: std_logic;
signal introdus3_uc: std_logic;
signal inroduCaractere_uc: std_logic;
signal liberOcupat_uc: std_logic;
signal selAfisor_uc: std_logic_vector (1 downto 0);
signal encmp: std_logic;
signal HEX,hex2,hex3: STD_LOGIC_VECTOR (3 downto 0);
signal SEG: STD_LOGIC_VECTOR (6 downto 0);


BEGIN

uc_1: UC port map(Mup,Mdown,Mreset,Madauga_cifra,Mclk,Mintrodus_3,rez_cifru,Mintrodu_cifre,liberOcupat_uc,selAfisor_uc,encmp);
counter_1: counter port map(Mclk,Mup,Mdown,Madauga_cifra,q_counter);
cifru_1: cifru port map(q_counter,selAfisor_uc,liberOcupat_uc,encmp,rez_cifru,HEX,hex2,hex3);
HEX2Seg_1: HEX2Seg port map(HEX,cif1);





END TypeArchitecture;

// VHDL entity portmapcounter, as the project stores it:
--------------------------------------------------------------------------------
-- Project :
-- File    :
-- Autor   :
-- Date    :
--
--------------------------------------------------------------------------------
-- Description :
--
--------------------------------------------------------------------------------

LIBRARY ieee;
USE ieee.std_logic_1164.all;

ENTITY portmapcounter IS
  PORT (
   mclk,mup,mdown,mreset: in std_logic;
   mQ: out std_logic_vector(3 downto 0)
    );
END portmapcounter;

--------------------------------------------------------------------------------
--Complete your VHDL description below
--------------------------------------------------------------------------------

ARCHITECTURE TypeArchitecture OF portmapcounter IS

component counter is 
  port(C,up,down,reset: in  std_logic;  
        Q : out std_logic_vector(3 downto 0));  
end component;

BEGIN

counter_test:counter port map(mclk,mup,mdown,mreset,mQ);


END TypeArchitecture;
